# Fritzing sketch sketch (saved by Fritzing 0.9.5d)

parts:
  WeMos_D1_Mini1 = WeMos D1 Mini
  Water_Level_Sensor1 = Water Level Sensor
  U1 = LIPO-1000mAh [package=lipo-1000]

nets:
  N1: WeMos_D1_Mini1.5V, U1.+
  N2: WeMos_D1_Mini1.A0, Water_Level_Sensor1.SIG
  N3: WeMos_D1_Mini1.D0, WeMos_D1_Mini1.RST
  N4: WeMos_D1_Mini1.D7, Water_Level_Sensor1.VCC
  N5: WeMos_D1_Mini1.G, Water_Level_Sensor1.GND, U1.-

custom parts:
  Water Level Sensor: A water level sensor. This sensor operates at 3V to 5V. The Sig (signal) pin outputs an analogue signal that is in proportion to the amount of water in contact with the sensor.
